# Fritzing sketch DoorBell (saved by Fritzing 0.9.3b)
perfboards: 1

parts:
  LM1 = RioRand LM2596
  IC1 = IC, DIP package, 16 pins [chip_label=L2930]
  Bauteil1 = Adafruit HUZZAH32 ESP32 Feather [part_number="Adafruit #3405"]
  U1 = Mini-360 DC-DC Buck converter [package=THT]
  R1 = Resistor [tolerance=±5% resistance=1.48k package=THT]
  Bauteil2 = Arduino MP3 Player Shield

nets:
  N1: LM1.Pin_0, IC1.pin8
  N2: LM1.Pin_1, IC1.pin4, IC1.pin5, IC1.pin12, IC1.pin13
  N3: LM1.Pin_2, U1.IN+
  N4: LM1.Pin_3, U1.IN-
  N5: IC1.pin1, IC1.pin9, IC1.pin16, U1.OUT-, Bauteil2.VCC
  N6: Bauteil1.IO21, R1.Pin_1
  N7: Bauteil1.3.3V, R1.Pin_0
  N8: U1.OUT+, Bauteil2.GND

notes:
  Amplifier: 12V In
  Amplifier: Left channel out
  Connector: Speaker
  Connector: 24V In
  Connector: Button in (Will get pulled to GND) - Check Color!
  Connector: ?? - Check Color!

custom parts:
  Mini-360 DC-DC Buck converter: Mini-360 DC-DC Buck converter. Tiny buck step down voltage converter, input voltage 4.75 to 23V output 1 to 17V adjustable. Available from ebay and the like.
